# Fritzing sketch EHME-1paramLine_4051_V (saved by Fritzing 0.9.3b)
perfboards: 2

parts:
  RE1 = Rotary Encoder [package=THT]
  RE2 = Rotary Encoder [package=THT]
  RE3 = Rotary Encoder [package=THT]
  RE4 = Rotary Encoder [package=THT]
  JP1 = Header 8 [package=1x08_smd]  # not connected
  4052 = DIP - 16 pins [chip_label=4051 package="DIP (Dual Inline) [THT]"]
  4052_2 = DIP - 16 pins [chip_label=4051 package="DIP (Dual Inline) [THT]"]
  4052_3 = DIP - 16 pins [chip_label=4051 package="DIP (Dual Inline) [THT]"]
  4052_4 = DIP - 16 pins [chip_label=4051 package="DIP (Dual Inline) [THT]"]
  4052_5 = DIP - 16 pins [chip_label=4051 package="DIP (Dual Inline) [THT]"]
  4052_6 = DIP - 16 pins [chip_label=4051 package="DIP (Dual Inline) [THT]"]
  RE5 = Rotary Encoder [package=THT]
  RE6 = Rotary Encoder [package=THT]
  RE7 = Rotary Encoder [package=THT]
  RE8 = Rotary Encoder [package=THT]

nets:
  N1: RE1.EncoderPinA, 4052_3.B
  N2: RE1.EncoderPinC, 4052_2.Common_X_Out/In
  N3: RE1.EncoderPinB, 4052.B
  N4: RE2.EncoderPinA, 4052_3.A
  N5: RE2.EncoderPinC, 4052_2.x0
  N6: RE2.EncoderPinB, 4052.A
  N7: RE3.EncoderPinA, 4052_3.x0
  N8: RE3.EncoderPinC, 4052_2.A
  N9: RE3.EncoderPinB, 4052.x0
  N10: RE4.EncoderPinA, 4052_3.Common_X_Out/In
  N11: RE4.EncoderPinC, 4052_2.B
  N12: RE4.EncoderPinB, 4052.Common_X_Out/In
  N13: 4052.y0, 4052_2.INH, 4052_3.INH, 4052_4.INH, 4052_5.INH, 4052_6.y0
  N14: 4052.y2, 4052_2.VEE, 4052_3.VEE, 4052_4.VEE, 4052_5.VEE, 4052_6.y2
  VSS: 4052.Common_Y_Out/In, 4052_2.VSS, 4052_3.VSS, 4052_4.VSS, 4052_5.VSS, 4052_6.Common_Y_Out/In
  N15: 4052.x1, 4052_2.x1, 4052_3.x1
  N16: 4052_4.B, RE7.EncoderPinC
  N17: 4052_4.A, RE8.EncoderPinC
  N18: 4052_4.x0, RE6.EncoderPinC
  N19: 4052_4.Common_X_Out/In, RE5.EncoderPinC
  N20: 4052_4.x1, 4052_5.x1, 4052_6.x1
  N21: 4052_5.B, RE5.EncoderPinA
  N22: 4052_5.A, RE6.EncoderPinA
  N23: 4052_5.x0, RE8.EncoderPinA
  N24: 4052_5.Common_X_Out/In, RE7.EncoderPinA
  N25: 4052_6.B, RE5.EncoderPinB
  N26: 4052_6.A, RE6.EncoderPinB
  N27: 4052_6.x0, RE8.EncoderPinB
  N28: 4052_6.Common_X_Out/In, RE7.EncoderPinB

custom parts:
  DIP - 16 pins: 4:1 Analog Multiplexer/Demultiplexer, Dual
